// Logisim project Jogo_Carrinho_de_Controle.circ as structural Verilog: 1 circuit, main circuit main
// w
module main (
);

  wire and_1_out, and_2_out, and_3_out, and_4_out, and_5_out, clock_1_out, or_1_out, w, y;
  wire [7:0] _33, _34, _35, _36, _37, _38, _39, _40, _41, _42, _43, _44, _45, _46, _47, _48, _49, _50, _51,
       _52, _53, _54, _55, _56, _57, _58, _59, _60, _61, _62, _63, _64, counter_1_q, rom_18_data,
       rom_19_data, rom_20_data, rom_21_data, rom_22_data, rom_23_data, rom_24_data, rom_25_data,
       rom_26_data, rom_27_data, rom_28_data, rom_29_data, rom_30_data, rom_31_data, rom_32_data,
       rom_33_data, rom_34_data, rom_35_data, rom_36_data, rom_37_data, rom_38_data, rom_39_data,
       rom_40_data, rom_41_data, rom_42_data, rom_43_data, rom_44_data, rom_45_data, rom_46_data,
       rom_47_data, rom_48_data, rom_49_data;
  wire [18:0] _01, _02, _03, _04, _05, _06, _07, _08, _09, _10, _11, _12, _13, _14, _15, _16, _17, _18, _19,
       _20, _21, _22, _23, _24, _25, _26, _27, _28, _29, _30, _31, _32, a, b, c, d, e, f, g, h, rom_1_data,
       rom_2_data, rom_3_data, rom_4_data, rom_5_data, rom_6_data, rom_7_data, rom_8_data, rom_9_data,
       rom_10_data, rom_11_data, rom_12_data, rom_13_data, rom_14_data, rom_15_data, rom_16_data, rom_17_data;

  DotMatrix #(.matrixcols(32), .matrixrows(8)) dotmatrix_1 (
    .col0(_64), .col1(_63), .col2(_62), .col3(_61), .col4(_60), .col5(_59), .col6(_58), .col7(_57),
    .col8(_56), .col9(_55), .col10(_54), .col11(_53), .col12(_52), .col13(_51), .col14(_50), .col15(_49),
    .col16(_48), .col17(_47), .col18(_46), .col19(_45), .col20(_44), .col21(_43), .col22(_42), .col23(_41),
    .col24(_40), .col25(_39), .col26(_38), .col27(_37), .col28(_36), .col29(_35), .col30(_34), .col31(_33));
  DotMatrix #(.matrixcols(8), .matrixrows(19)) dotmatrix_2 (
    .col0(a), .col1(b), .col2(c), .col3(d), .col4(e), .col5(f), .col6(g), .col7(h));
  DotMatrix #(.matrixcols(32), .matrixrows(19)) dotmatrix_3 (
    .col0(_32), .col1(_31), .col2(_30), .col3(_29), .col4(_28), .col5(_27), .col6(_26), .col7(_25),
    .col8(_24), .col9(_23), .col10(_22), .col11(_21), .col12(_20), .col13(_19), .col14(_18), .col15(_17),
    .col16(_16), .col17(_15), .col18(_14), .col19(_13), .col20(_12), .col21(_11), .col22(_10), .col23(_09),
    .col24(_08), .col25(_07), .col26(_06), .col27(_05), .col28(_04), .col29(_03), .col30(_02), .col31(_01));
  Button Reset (.out(w));
  Button Controle_do_carro (.out(y));
  Counter #(.trigger("falling")) counter_1 (
    .Q(counter_1_q), .clk(clock_1_out), .clr(w));  // open: load, D, count, carry
  Clock clock_1 (.out(clock_1_out));
  ROM #(.dataWidth(19)) rom_1 (.addr({8{1'b1}}), .data(rom_1_data));  // open: sel
  ROM #(.dataWidth(19)) rom_2 (.addr({8{1'b1}}), .data(rom_2_data));  // open: sel
  ROM #(.dataWidth(19)) rom_3 (.addr({8{1'b1}}), .data(rom_3_data));  // open: sel
  ROM #(.dataWidth(19)) rom_4 (.addr({8{1'b1}}), .data(rom_4_data));  // open: sel
  ROM #(.dataWidth(19)) rom_5 (.addr({8{1'b1}}), .data(rom_5_data));  // open: sel
  ROM #(.dataWidth(19)) rom_6 (.addr({8{1'b1}}), .data(rom_6_data));  // open: sel
  ROM #(.dataWidth(19)) rom_7 (.addr({8{1'b1}}), .data(rom_7_data));  // open: sel
  ROM #(.dataWidth(19)) rom_8 (.addr({8{1'b1}}), .data(rom_8_data));  // open: sel
  ROM #(.dataWidth(19)) rom_9 (.addr({8{1'b1}}), .data(rom_9_data));  // open: sel
  ROM #(.dataWidth(19)) rom_10 (.addr({8{1'b1}}), .data(rom_10_data));  // open: sel
  ROM #(.dataWidth(19)) rom_11 (.addr({8{1'b1}}), .data(rom_11_data));  // open: sel
  ROM #(.dataWidth(19)) rom_12 (.addr({8{1'b1}}), .data(rom_12_data));  // open: sel
  ROM #(.dataWidth(19)) rom_13 (.addr({8{1'b1}}), .data(rom_13_data));  // open: sel
  ROM #(.dataWidth(19)) rom_14 (.addr({8{1'b1}}), .data(rom_14_data));  // open: sel
  ROM #(.dataWidth(19)) rom_15 (.addr({8{1'b1}}), .data(rom_15_data));  // open: sel
  ROM #(.dataWidth(19)) rom_16 (.addr({8{1'b1}}), .data(rom_16_data));  // open: sel
  Shift_Register #(.width(19), .length(32)) Registrador_de_deslocamento___Obstaculos (
    .in(rom_17_data), .clk(clock_1_out), .clr(w), .q0(_01), .q1(_02), .q2(_03), .q3(_04), .q4(_05), .q5(_06),
    .q6(_07), .q7(_08), .q8(_09), .q9(_10), .q10(_11), .q11(_12), .q12(_13), .q13(_14), .q14(_15), .q15(_16),
    .q16(_17), .q17(_18), .q18(_19), .q19(_20), .q20(_21), .q21(_22), .q22(_23), .q23(_24), .q24(_25),
    .q25(_26), .q26(_27), .q27(_28), .q28(_29), .q29(_30), .q30(_31), .q31(_32));  // open: shift, out, load, d0, d1, d2, d3, d4, d5, d6, d7, d8, d9, d10, d11, d12, d13, d14, d15, d16, d17, d18, d19, d20, d21, d22, d23, d24, d25, d26, d27, d28, d29, d30, d31
  ROM #(.dataWidth(19)) rom_17 (.addr(counter_1_q), .data(rom_17_data));  // open: sel
  and and_1 (and_1_out, _30[1], f[1], f[5], _30[5]);
  and and_2 (and_2_out, _30[4], _30[8], f[1], f[5]);
  and and_3 (and_3_out, _30[0], _30[4], f[1], f[5]);
  and and_4 (and_4_out, _30[10], _30[14], f[13], f[17]);
  and and_5 (and_5_out, _30[13], _30[17], f[13], f[17]);
  Multiplexer #(.width(19)) multiplexer_1 (.in0(rom_1_data), .in1(rom_2_data), .out(a), .sel(y));  // open: en
  Multiplexer #(.width(19)) multiplexer_2 (.in0(rom_3_data), .in1(rom_4_data), .out(b), .sel(y));  // open: en
  Multiplexer #(.width(19)) multiplexer_3 (.in0(rom_5_data), .in1(rom_6_data), .out(c), .sel(y));  // open: en
  Multiplexer #(.width(19)) multiplexer_4 (.in0(rom_7_data), .in1(rom_8_data), .out(d), .sel(y));  // open: en
  Multiplexer #(.width(19)) multiplexer_5 (.in0(rom_9_data), .in1(rom_10_data), .out(e), .sel(y));  // open: en
  Multiplexer #(.width(19)) multiplexer_6 (.in0(rom_11_data), .in1(rom_12_data), .out(f), .sel(y));  // open: en
  Multiplexer #(.width(19)) multiplexer_7 (.in0(rom_13_data), .in1(rom_14_data), .out(g), .sel(y));  // open: en
  Multiplexer #(.width(19)) multiplexer_8 (.in0(rom_15_data), .in1(rom_16_data), .out(h), .sel(y));  // open: en
  or or_1 (or_1_out, and_1_out, and_2_out, and_3_out, and_4_out, and_5_out);
  Multiplexer #(.width(8)) multiplexer_9 (.in0({8{1'b0}}), .in1(rom_18_data), .out(_64), .sel(or_1_out));  // open: en
  ROM rom_18 (.addr({8{1'b0}}), .data(rom_18_data));  // open: sel
  Multiplexer #(.width(8)) multiplexer_10 (.in0({8{1'b0}}), .in1(rom_19_data), .out(_63), .sel(or_1_out));  // open: en
  ROM rom_19 (.addr({8{1'b0}}), .data(rom_19_data));  // open: sel
  Multiplexer #(.width(8)) multiplexer_11 (.in0({8{1'b0}}), .in1(rom_20_data), .out(_62), .sel(or_1_out));  // open: en
  ROM rom_20 (.addr({8{1'b0}}), .data(rom_20_data));  // open: sel
  Multiplexer #(.width(8)) multiplexer_12 (.in0({8{1'b0}}), .in1(rom_21_data), .out(_61), .sel(or_1_out));  // open: en
  ROM rom_21 (.addr({8{1'b0}}), .data(rom_21_data));  // open: sel
  Multiplexer #(.width(8)) multiplexer_13 (.in0({8{1'b0}}), .in1(rom_22_data), .out(_60), .sel(or_1_out));  // open: en
  ROM rom_22 (.addr({8{1'b0}}), .data(rom_22_data));  // open: sel
  Multiplexer #(.width(8)) multiplexer_14 (.in0({8{1'b0}}), .in1(rom_23_data), .out(_59), .sel(or_1_out));  // open: en
  ROM rom_23 (.addr({8{1'b0}}), .data(rom_23_data));  // open: sel
  Multiplexer #(.width(8)) multiplexer_15 (.in0({8{1'b0}}), .in1(rom_24_data), .out(_58), .sel(or_1_out));  // open: en
  ROM rom_24 (.addr({8{1'b0}}), .data(rom_24_data));  // open: sel
  Multiplexer #(.width(8)) multiplexer_16 (.in0({8{1'b0}}), .in1(rom_25_data), .out(_57), .sel(or_1_out));  // open: en
  ROM rom_25 (.addr({8{1'b0}}), .data(rom_25_data));  // open: sel
  Multiplexer #(.width(8)) multiplexer_17 (.in0({8{1'b0}}), .in1(rom_26_data), .out(_56), .sel(or_1_out));  // open: en
  ROM rom_26 (.addr({8{1'b0}}), .data(rom_26_data));  // open: sel
  Multiplexer #(.width(8)) multiplexer_18 (.in0({8{1'b0}}), .in1(rom_27_data), .out(_55), .sel(or_1_out));  // open: en
  ROM rom_27 (.addr({8{1'b0}}), .data(rom_27_data));  // open: sel
  Multiplexer #(.width(8)) multiplexer_19 (.in0({8{1'b0}}), .in1(rom_28_data), .out(_54), .sel(or_1_out));  // open: en
  ROM rom_28 (.addr({8{1'b0}}), .data(rom_28_data));  // open: sel
  Multiplexer #(.width(8)) multiplexer_20 (.in0({8{1'b0}}), .in1(rom_29_data), .out(_53), .sel(or_1_out));  // open: en
  ROM rom_29 (.addr({8{1'b0}}), .data(rom_29_data));  // open: sel
  Multiplexer #(.width(8)) multiplexer_21 (.in0({8{1'b0}}), .in1(rom_30_data), .out(_52), .sel(or_1_out));  // open: en
  ROM rom_30 (.addr({8{1'b0}}), .data(rom_30_data));  // open: sel
  Multiplexer #(.width(8)) multiplexer_22 (.in0({8{1'b0}}), .in1(rom_31_data), .out(_51), .sel(or_1_out));  // open: en
  ROM rom_31 (.addr({8{1'b0}}), .data(rom_31_data));  // open: sel
  Multiplexer #(.width(8)) multiplexer_23 (.in0({8{1'b0}}), .in1(rom_32_data), .out(_50), .sel(or_1_out));  // open: en
  ROM rom_32 (.addr({8{1'b0}}), .data(rom_32_data));  // open: sel
  Multiplexer #(.width(8)) multiplexer_24 (.in0({8{1'b0}}), .in1(rom_33_data), .out(_49), .sel(or_1_out));  // open: en
  ROM rom_33 (.addr({8{1'b0}}), .data(rom_33_data));  // open: sel
  Multiplexer #(.width(8)) multiplexer_25 (.in0({8{1'b0}}), .in1(rom_34_data), .out(_48), .sel(or_1_out));  // open: en
  ROM rom_34 (.addr({8{1'b0}}), .data(rom_34_data));  // open: sel
  Multiplexer #(.width(8)) multiplexer_26 (.in0({8{1'b0}}), .in1(rom_35_data), .out(_47), .sel(or_1_out));  // open: en
  ROM rom_35 (.addr({8{1'b0}}), .data(rom_35_data));  // open: sel
  Multiplexer #(.width(8)) multiplexer_27 (.in0({8{1'b0}}), .in1(rom_36_data), .out(_46), .sel(or_1_out));  // open: en
  ROM rom_36 (.addr({8{1'b0}}), .data(rom_36_data));  // open: sel
  Multiplexer #(.width(8)) multiplexer_28 (.in0({8{1'b0}}), .in1(rom_37_data), .out(_45), .sel(or_1_out));  // open: en
  ROM rom_37 (.addr({8{1'b0}}), .data(rom_37_data));  // open: sel
  Multiplexer #(.width(8)) multiplexer_29 (.in0({8{1'b0}}), .in1(rom_38_data), .out(_44), .sel(or_1_out));  // open: en
  ROM rom_38 (.addr({8{1'b0}}), .data(rom_38_data));  // open: sel
  Multiplexer #(.width(8)) multiplexer_30 (.in0({8{1'b0}}), .in1(rom_39_data), .out(_43), .sel(or_1_out));  // open: en
  ROM rom_39 (.addr({8{1'b0}}), .data(rom_39_data));  // open: sel
  Multiplexer #(.width(8)) multiplexer_31 (.in0({8{1'b0}}), .in1(rom_40_data), .out(_42), .sel(or_1_out));  // open: en
  ROM rom_40 (.addr({8{1'b0}}), .data(rom_40_data));  // open: sel
  Multiplexer #(.width(8)) multiplexer_32 (.in0({8{1'b0}}), .in1(rom_41_data), .out(_41), .sel(or_1_out));  // open: en
  ROM rom_41 (.addr({8{1'b0}}), .data(rom_41_data));  // open: sel
  Multiplexer #(.width(8)) multiplexer_33 (.in0({8{1'b0}}), .in1(rom_42_data), .out(_40), .sel(or_1_out));  // open: en
  ROM rom_42 (.addr({8{1'b0}}), .data(rom_42_data));  // open: sel
  Multiplexer #(.width(8)) multiplexer_34 (.in0({8{1'b0}}), .in1(rom_43_data), .out(_39), .sel(or_1_out));  // open: en
  ROM rom_43 (.addr({8{1'b0}}), .data(rom_43_data));  // open: sel
  Multiplexer #(.width(8)) multiplexer_35 (.in0({8{1'b0}}), .in1(rom_44_data), .out(_38), .sel(or_1_out));  // open: en
  ROM rom_44 (.addr({8{1'b0}}), .data(rom_44_data));  // open: sel
  Multiplexer #(.width(8)) multiplexer_36 (.in0({8{1'b0}}), .in1(rom_45_data), .out(_37), .sel(or_1_out));  // open: en
  ROM rom_45 (.addr({8{1'b0}}), .data(rom_45_data));  // open: sel
  Multiplexer #(.width(8)) multiplexer_37 (.in0({8{1'b0}}), .in1(rom_46_data), .out(_36), .sel(or_1_out));  // open: en
  ROM rom_46 (.addr({8{1'b0}}), .data(rom_46_data));  // open: sel
  Multiplexer #(.width(8)) multiplexer_38 (.in0({8{1'b0}}), .in1(rom_47_data), .out(_35), .sel(or_1_out));  // open: en
  ROM rom_47 (.addr({8{1'b0}}), .data(rom_47_data));  // open: sel
  Multiplexer #(.width(8)) multiplexer_39 (.in0({8{1'b0}}), .in1(rom_48_data), .out(_34), .sel(or_1_out));  // open: en
  ROM rom_48 (.addr({8{1'b0}}), .data(rom_48_data));  // open: sel
  Multiplexer #(.width(8)) multiplexer_40 (.in0({8{1'b0}}), .in1(rom_49_data), .out(_33), .sel(or_1_out));  // open: en
  ROM rom_49 (.addr({8{1'b0}}), .data(rom_49_data));  // open: sel

  // Other names for the same wires on the sheet: x[18:0] = f; z[18:0] = _30

  // Notes on the sheet:
  //   Comparador de colisao
  //   Memoria dos carrinhos
  //   contents of rom_1 (hex, n*v repeats v):
  //   255*0 36
  //   contents of rom_2 (hex, n*v repeats v):
  //   255*0 36000
  //   contents of rom_3 (hex, n*v repeats v):
  //   255*0 36
  //   contents of rom_4 (hex, n*v repeats v):
  //   255*0 36000
  //   contents of rom_5 (hex, n*v repeats v):
  //   255*0 1c
  //   contents of rom_6 (hex, n*v repeats v):
  //   255*0 1c000
  //   contents of rom_7 (hex, n*v repeats v):
  //   255*0 1c
  //   contents of rom_8 (hex, n*v repeats v):
  //   255*0 1c000
  //   contents of rom_9 (hex, n*v repeats v):
  //   255*0 36
  //   contents of rom_10 (hex, n*v repeats v):
  //   255*0 36000
  //   contents of rom_11 (hex, n*v repeats v):
  //   255*0 3e
  //   contents of rom_12 (hex, n*v repeats v):
  //   255*0 3e000
  //   contents of rom_13 (hex, n*v repeats v):
  //   255*0 1c
  //   contents of rom_14 (hex, n*v repeats v):
  //   255*0 1c000
  //   contents of rom_15 (hex, n*v repeats v):
  //   255*0 8
  //   contents of rom_16 (hex, n*v repeats v):
  //   255*0 8000
  //   contents of rom_17 (hex, n*v repeats v):
  //   8 1c 3e 13*0 40 e0 1f0 13*0 1000 3800 7c00 13*0 400 e00 1f00 13*0 8000 1c000 3e000 13*0 4 e 1f 13*0
  //   40 e0 1f0 13*0 8 1c 3e 13*0 400 e00 1f00 13*0 40 e0 1f0 13*0 8000 1c000 3e000 13*0 8 1c 3e 13*0 400
  //   e00 1f00 13*0 8000 1c000 3e000 13*0 8 1c 3e 13*0 1000 3800 7c00
  //   Memoria: Game Over
  //   contents of rom_18 (hex, n*v repeats v):
  //   7e
  //   contents of rom_19 (hex, n*v repeats v):
  //   81
  //   contents of rom_20 (hex, n*v repeats v):
  //   89
  //   contents of rom_21 (hex, n*v repeats v):
  //   8e
  //   contents of rom_23 (hex, n*v repeats v):
  //   7f
  //   contents of rom_24 (hex, n*v repeats v):
  //   88
  //   contents of rom_25 (hex, n*v repeats v):
  //   7f
  //   contents of rom_27 (hex, n*v repeats v):
  //   ff
  //   contents of rom_28 (hex, n*v repeats v):
  //   20
  //   contents of rom_29 (hex, n*v repeats v):
  //   ff
  //   contents of rom_31 (hex, n*v repeats v):
  //   ff
  //   contents of rom_32 (hex, n*v repeats v):
  //   89
  //   contents of rom_33 (hex, n*v repeats v):
  //   81
  //   contents of rom_35 (hex, n*v repeats v):
  //   7e
  //   contents of rom_36 (hex, n*v repeats v):
  //   81
  //   contents of rom_37 (hex, n*v repeats v):
  //   7e
  //   contents of rom_39 (hex, n*v repeats v):
  //   fe
  //   contents of rom_40 (hex, n*v repeats v):
  //   1
  //   contents of rom_41 (hex, n*v repeats v):
  //   fe
  //   contents of rom_43 (hex, n*v repeats v):
  //   7e
  //   contents of rom_44 (hex, n*v repeats v):
  //   89
  //   contents of rom_45 (hex, n*v repeats v):
  //   81
  //   contents of rom_47 (hex, n*v repeats v):
  //   ff
  //   contents of rom_48 (hex, n*v repeats v):
  //   88
  //   contents of rom_49 (hex, n*v repeats v):
  //   f7
endmodule
